# Fritzing sketch wiring_counter_with_arcade_buttons (saved by Fritzing 1.0.5)

parts:
  RS485_module1 = RS485 Module (MAX3485)
  BUTTON1 = Arcade Button (red)
  BUTTON2 = Arcade Button (green)
  LED1 = LEDs [package=led10mm]
  LED2 = LEDs [package=led10mm]
  Part2 = Arduino Nano (Rev3.0) (ICSP)
  Grove1 = Grove 4 Digit Display
  Power_plug1 = Power plug
  U1 = BNC socket [package=bnc]
  J1 = Piezo Speaker
  R1 = Resistor [tolerance=±1% resistance=220 package="2010 [SMD]"]
  R2 = Resistor [tolerance=±1% resistance=220 package="2010 [SMD]"]
  R3 = Resistor [tolerance=±1% resistance=100 package="2010 [SMD]"]

nets:
  GND: RS485_module1.GND, BUTTON1.no_name_yet#1, BUTTON2.no_name_yet#1, LED1.A, LED2.C, Part2.GND, Grove1.GND, Power_plug1.GND, J1.pin1
  N1: RS485_module1.A, U1.GND
  N2: RS485_module1.B, U1.OUT
  VCC: RS485_module1.VCC, Part2.5V, Grove1.VCC
  N3: RS485_module1.RO, Part2.D10
  N4: RS485_module1.RE, Part2.D9
  N5: RS485_module1.DI, Part2.D8
  N6: BUTTON1.no_name_yet#2, Part2.D5
  N7: BUTTON2.no_name_yet#2, Part2.D2
  N8: LED1.C, R2.Pin_0
  N9: LED2.A, R1.Pin_0
  N10: Part2.D3, R1.Pin_1
  N11: Part2.D4, R2.Pin_1
  N12: Part2.D6, R3.Pin_1
  VIN: Part2.VIN, Power_plug1.VCC
  N13: Part2.A5, Grove1.CLK
  N14: Part2.A4, Grove1.DIO
  N15: J1.pin2, R3.Pin_0

notes:
  220 Ω
  100 Ω

custom parts:
  RS485 Module (MAX3485): Commercially available RS485 to RS232 TTL Module
  Arcade Button (red): Adafruit Arcade Button (red)
  Arcade Button (green): Adafruit Arcade Button (green)
